# Fritzing sketch RC_fritz_diagram_bb (saved by Fritzing 0.9.10b)
breadboards: 1

parts:
  Mod1 = flyskyr6b
  Part1 = Adafruit Metro with Headers [part_number="Adafruit #2488"]
  Part3 = TXB0108 8-channel Bi-directional Logic Level Converter

nets:
  N1: Mod1.CH1, Part3.B1
  VCC: Mod1.VCC, Mod1.BAT+, Part1.+5V, Part3.B8
  GND: Mod1.connector14, Mod1.GND, Part1.GND, Part3.B6, Part3.B7, Part3.GND
  N2: Part1.IO5, Part3.VCCA
  N3: Part1.IO2, Part3.A8
  N4: Part3.OE, Part3.A7, Part3.A6

custom parts:
  flyskyr6b: flysky r6b 6ch rc receiver module. Pcb view is 3*7 header pins, 3 female headers will let the board plug in to the receiver, or connect via wires as you choose.
  Adafruit Metro with Headers: We sure love the ATmega328 here at Adafruit, and we use them a lot for our own projects. The processor has plenty of GPIO, Analog inputs, hardware UART SPI and I2C, timers and PWM galore - just enough for most simple projects. When we need to go small, we use a Pro Trinket 3V or 5V, but when size isn't as much of a concern, and an USB-serial converter is required, we reach for an Adafruit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
  TXB0108 8-channel Bi-directional Logic Level Converter: Because the Arduino (and Basic Stamp) are 5V devices, and most modern sensors, displays, flash cards and modes are 3.3V-only, many makers find that they need to perform level shifting/conversion to protect the 3.3V device from 5V. Although one can use resistors to make a divider, for high speed transfers, the resistors can add a lot of slew and cause havoc that is tough to debug. For that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
