# Fritzing sketch simple motor gearbox (saved by Fritzing 0.9.10b)
breadboards: 1

parts:
  Part1 = Adafruit Metro with Headers [part_number="Adafruit #2488"]
  Mod1 = flyskyr6b
  M2 = roboclaw_2x45a

nets:
  N1: Part1.MOSI, M2.S1-Sig
  N2: Part1.SS, M2.S2-Sig
  N3: Part1.IO3, Mod1.CH6
  N4: Part1.IO2, Mod1.CH5
  N5: Part1.IO1, Mod1.CH2
  N6: Part1.IO0, Mod1.CH1
  N7: Part1.+5V, Mod1.BAT+
  GND: Part1.GND, Mod1.GND, M2.EN2_-, M2.S1-GND, M2.S5-GND

notes:
  FlySky

custom parts:
  Adafruit Metro with Headers: We sure love the ATmega328 here at Adafruit, and we use them a lot for our own projects. The processor has plenty of GPIO, Analog inputs, hardware UART SPI and I2C, timers and PWM galore - just enough for most simple projects. When we need to go small, we use a Pro Trinket 3V or 5V, but when size isn't as much of a concern, and an USB-serial converter is required, we reach for an Adafruit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
  flyskyr6b: flysky r6b 6ch rc receiver module. Pcb view is 3*7 header pins, 3 female headers will let the board plug in to the receiver, or connect via wires as you choose.
  roboclaw_2x45a: Roboclaw 2x45 motor driver.
