# Fritzing sketch mars_rover (saved by Fritzing 0.9.10b)
breadboards: 1

parts:
  C1 = Electrolytic Capacitor [capacitance=1µF voltage=35V package="100 mil [THT, electrolytic]"]
  Part1 = Adafruit Metro with Headers [part_number="Adafruit #2488"]
  C3 = Capacitor [package=cap-pth-small-kit]
  J2 = Basic Servo
  J1 = Basic Servo

nets:
  VCC: C1.-, Part1.+5V, C3.1, J2.vcc, J1.vcc
  GND: C1.+, Part1.GND, C3.2, J2.gnd, J1.gnd
  N1: Part1.IO1, J1.pulse
  N2: Part1.IO0, J2.pulse

custom parts:
  Adafruit Metro with Headers: We sure love the ATmega328 here at Adafruit, and we use them a lot for our own projects. The processor has plenty of GPIO, Analog inputs, hardware UART SPI and I2C, timers and PWM galore - just enough for most simple projects. When we need to go small, we use a Pro Trinket 3V or 5V, but when size isn't as much of a concern, and an USB-serial converter is required, we reach for an Adafruit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
