# Fritzing sketch multiple_i2c (saved by Fritzing 0.9.10b)
breadboards: 1

parts:
  Part1 = Adafruit Metro with Headers [part_number="Adafruit #2488"]
  Part2 = OLED Monochrome 128x64 1.3 inch [part_number=938]
  Part3 = Adafruit APDS-9960 [part_number="Adafruit #3595"]

nets:
  N1: Part1.AD5/SCL, Part2.SCLK_SCK, Part3.SCL
  N2: Part1.AD4/SDA, Part2.MOSI_SDA, Part3.SDA
  VIN: Part1.3.3V, Part2.VIN, Part3.VIN
  GND: Part1.GND, Part2.GND, Part3.GND

custom parts:
  Adafruit Metro with Headers: We sure love the ATmega328 here at Adafruit, and we use them a lot for our own projects. The processor has plenty of GPIO, Analog inputs, hardware UART SPI and I2C, timers and PWM galore - just enough for most simple projects. When we need to go small, we use a Pro Trinket 3V or 5V, but when size isn't as much of a concern, and an USB-serial converter is required, we reach for an Adafruit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
  OLED Monochrome 128x64 1.3 inch: These displays are small, only about 1.3" diagonal, but very readable due to the high contrast of an OLED display. This display is made of 128x64 individual white OLED pixels, each one is turned on or off by the controller chip. Because the display makes its own light, no backlight is required. This reduces the power required to run the OLED and is why the display has such high contrast; we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
  Adafruit APDS-9960: The APDS9960 from Avago Technologies has an integrated IR LED and driver, along with four directional photodiodes that sense reflected IR energy from the LED. It's proximity detection feature allows it to measure the distance an object is from the front of the sensor (up to a few centimeters) with 8 bit resolution. Since there are four IR sensors, you can measure the changes in light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
