# Fritzing sketch challenge_1_fritzing_diagram (saved by Fritzing 0.9.10b)
breadboards: 1

parts:
  Part1 = Adafruit Metro with Headers [part_number="Adafruit #2488"]
  S1 = Pushbutton [package="[SMD]"]
  R1 = Resistor [tolerance=±5% resistance=220 package="0402 [SMD]"]
  LED1 = LED - 5mm [color="Red (633nm)" current=0.030 package="5 mm [THT]"]
  LED2 = LED - 5mm [color="Green (560nm)" current=0.030 package="5 mm [THT]"]
  R2 = Resistor [tolerance=±5% resistance=220 package="0402 [SMD]"]
  R3 = Resistor [tolerance=±5% resistance=220 package="0402 [SMD]"]
  HC-SR04_Sensor_1 = HC-SR04 Ultrasonic Distance Sensor
  Part2 = 16 NeoPixel Ring [part_number=1463]
  R4 = Rotary Potentiometer (Large) [maximum_resistance=100kΩ knob_status=50% power=0.5W package=THT]
  Part3 = OLED Monochrome 128x64 0.96 inch [part_number=326]

nets:
  N1: Part1.AD1, R4.wiper
  N2: Part1.AD5/SCL, Part3.SCLK_SCK
  N3: Part1.AD4/SDA, Part3.MOSI_SDA
  N4: Part1.MISO, S1.Pin_1, S1.Pin_2
  N5: Part1.MOSI, R2.Pin_1
  N6: Part1.SS, R3.Pin_1
  N7: Part1.IO8, Part2.IN
  N8: Part1.IO7, HC-SR04_Sensor_1.TRIG, HC-SR04_Sensor_1.ECHO
  3.3V: Part1.3.3V, S1.Pin_3, S1.Pin_4, R1.Pin_0, Part3.3.3V
  +5V: Part1.+5V, HC-SR04_Sensor_1.VCC, Part2.VDD, R4.leg1
  GND: Part1.GND, R1.Pin_1, LED1.cathode, LED2.cathode, HC-SR04_Sensor_1.GND, Part2.GND, R4.leg2, Part3.GND
  N9: LED1.anode, R2.Pin_0
  N10: LED2.anode, R3.Pin_0

custom parts:
  Adafruit Metro with Headers: We sure love the ATmega328 here at Adafruit, and we use them a lot for our own projects. The processor has plenty of GPIO, Analog inputs, hardware UART SPI and I2C, timers and PWM galore - just enough for most simple projects. When we need to go small, we use a Pro Trinket 3V or 5V, but when size isn't as much of a concern, and an USB-serial converter is required, we reach for an Adafruit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
  16 NeoPixel Ring: 16 ultra bright smart LED NeoPixels are arranged in a circle with 1.75" (44.5mm) outer diameter. The rings are 'chainable' - connect the output pin of one to the input pin of another. Use only one microcontroller pin to control as many as you can chain together! Each LED is addressable as the driver chip is inside the LED. Each one has ~18mA constant current drive so the color will be very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
  OLED Monochrome 128x64 0.96 inch: These displays are small, only about 1" diameter, but very readable due to the high contrast of an OLED display. This display is made of 128x64 individual white OLED pixels, each one is turned on or off by the controller chip. Because the display makes its own light, no backlight is required. This reduces the power required to run the OLED and is why the display has such high contrast; we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

// code stored in the sketch: Untitled.ino

